// Digital circuit crc.dig as structural Verilog
module crc (
  input  [31:0] crc_in,
  input  [31:0] table_in,
  input  [3:0] limit,
  output [31:0] crc_out,
  output [3:0] limit_out
);

  wire comparator_1_gt, comparator_2_gt;
  wire [3:0] sub_1_s;
  wire [31:0] xor_1_out;

  Sub #(.Bits(4)) sub_1 (.a(limit), .b(4'b0001), .c_i(1'b0), .s(sub_1_s));  // open: c_o
  Comparator #(.Bits(4)) comparator_1 (.a(limit), .b(4'b0000), .gt(comparator_1_gt));  // open: eq, lt
  assign xor_1_out = {{8{1'b0}}, crc_in[31:8]} ^ table_in;  // XOr xor_1, 32 bits wide
  Comparator #(.Bits(4)) comparator_2 (.a(limit), .b(4'b0000), .gt(comparator_2_gt));  // open: eq, lt
  Multiplexer #(.Bits(4)) multiplexer_1 (.sel(comparator_2_gt), .in_0(4'b0000), .in_1(sub_1_s), .out(limit_out));
  Multiplexer #(.Bits(32)) multiplexer_2 (.sel(comparator_1_gt), .in_0(crc_in), .in_1(xor_1_out), .out(crc_out));
endmodule
