// Digital circuit dataLimit.dig as structural Verilog
module dataLimit (
  input  [63:0] data,
  output [3:0] limit,
  output [7:0] _56_63,
  output [7:0] _48_55,
  output [7:0] _40_47,
  output [7:0] _32_37,
  output [7:0] _24_31,
  output [7:0] _16_23,
  output [7:0] _8_15,
  output [7:0] _0_7
);

  wire comparator_1_gt, comparator_2_gt, comparator_3_gt, comparator_4_gt, comparator_5_gt, comparator_6_gt,
       comparator_7_gt, comparator_8_gt;
  wire [1:0] add_1_c_o, add_2_c_o, add_3_s, add_4_s, add_5_s, add_6_s;
  wire [2:2] add_5_c_o, add_6_c_o;

  Comparator #(.Bits(8)) comparator_1 (.a(data[63:56]), .b({8{1'b0}}), .gt(comparator_1_gt));  // open: eq, lt
  Comparator #(.Bits(8)) comparator_2 (.a(data[55:48]), .b({8{1'b0}}), .gt(comparator_2_gt));  // open: eq, lt
  Comparator #(.Bits(8)) comparator_3 (.a(data[47:40]), .b({8{1'b0}}), .gt(comparator_3_gt));  // open: eq, lt
  Comparator #(.Bits(8)) comparator_4 (.a(data[39:32]), .b({8{1'b0}}), .gt(comparator_4_gt));  // open: eq, lt
  Comparator #(.Bits(8)) comparator_5 (.a(data[31:24]), .b({8{1'b0}}), .gt(comparator_5_gt));  // open: eq, lt
  Comparator #(.Bits(8)) comparator_6 (.a(data[23:16]), .b({8{1'b0}}), .gt(comparator_6_gt));  // open: eq, lt
  Comparator #(.Bits(8)) comparator_7 (.a(data[15:8]), .b({8{1'b0}}), .gt(comparator_7_gt));  // open: eq, lt
  Comparator #(.Bits(8)) comparator_8 (.a(data[7:0]), .b({8{1'b0}}), .gt(comparator_8_gt));  // open: eq, lt
  Add add_1 (.a(comparator_1_gt), .b(comparator_2_gt), .c_i(1'b0), .s(add_1_c_o[0]), .c_o(add_1_c_o[1]));
  Add add_2 (.a(comparator_3_gt), .b(comparator_4_gt), .c_i(1'b0), .s(add_2_c_o[0]), .c_o(add_2_c_o[1]));
  Add add_3 (.a(comparator_5_gt), .b(comparator_6_gt), .c_i(1'b0), .s(add_3_s[0]), .c_o(add_3_s[1]));
  Add add_4 (.a(comparator_7_gt), .b(comparator_8_gt), .c_i(1'b0), .s(add_4_s[0]), .c_o(add_4_s[1]));
  Add #(.Bits(2)) add_5 (.a(add_1_c_o), .b(add_2_c_o), .c_i(1'b0), .s(add_5_s), .c_o(add_5_c_o[2]));
  Add #(.Bits(2)) add_6 (.a(add_3_s), .b(add_4_s), .c_i(1'b0), .s(add_6_s), .c_o(add_6_c_o[2]));
  Add #(.Bits(3)) add_7 (
    .a({add_5_c_o[2], add_5_s}), .b({add_6_c_o[2], add_6_s}), .c_i(1'b0), .s(limit[2:0]), .c_o(limit[3]));

  assign _0_7 = data[7:0];
  assign _8_15 = data[15:8];
  assign _16_23 = data[23:16];
  assign _24_31 = data[31:24];
  assign _32_37 = data[39:32];
  assign _40_47 = data[47:40];
  assign _48_55 = data[55:48];
  assign _56_63 = data[63:56];
endmodule
