// Digital circuit tableAddress.dig as structural Verilog
module tableAddress (
  input  [31:0] crc_in,
  input  [7:0] data_in,
  output [7:0] table_address
);

  assign table_address = data_in ^ crc_in[7:0];  // XOr xor_1, 8 bits wide
endmodule
